// Logisim project cpu.circ as structural Verilog: 1 circuit, main circuit main
module main (
);

  wire and_1_out, and_2_out, and_3_out, and_4_out, and_5_out, and_6_out, clock_1_out, comparator_1_eq,
       comparator_1_gt, comparator_2_lt, j_k_ff_1_q, j_k_ff_1_qn, j_k_ff_2_q, MODE_q, not_1_out, not_2_out,
       not_3_out, not_4_out, not_5_out, not_6_out, not_7_out, not_8_out, not_9_out, not_10_out, not_11_out,
       not_12_out, not_13_out, not_14_out, not_15_out, not_16_out, not_17_out, not_18_out, undriven,
       undriven_2;
  wire [15:0] adder_1_out, adder_2_out, IR0_q, MAR_q, MBR_q, MDR_q, MLR_q, multiplexer_1_out, PC_q,
       ram_1_dout;

  Clock clock_1 (.out(clock_1_out));
  J_K_Flip_Flop j_k_ff_1 (
    .J(1'b1), .K(1'b1), .clk(clock_1_out), .Q(j_k_ff_1_q), .Qn(j_k_ff_1_qn));  // open: preset, reset
  not not_1 (not_1_out, j_k_ff_1_q);
  and and_1 (and_1_out, not_1_out, not_2_out);
  J_K_Flip_Flop j_k_ff_2 (.J(1'b1), .K(1'b1), .clk(j_k_ff_1_qn), .Q(j_k_ff_2_q));  // open: Qn, preset, reset
  and and_2 (and_2_out, not_2_out, j_k_ff_1_q);
  and and_3 (and_3_out, not_1_out, j_k_ff_2_q);
  and and_4 (and_4_out, j_k_ff_2_q, j_k_ff_1_q);
  not not_2 (not_2_out, j_k_ff_2_q);
  Register #(.width(16)) PC (.D(adder_1_out), .en(and_1_out), .clk(clock_1_out), .Q(PC_q));  // open: clr
  Adder #(.width(16)) adder_1 (.a(PC_q), .b(16'h1), .out(adder_1_out));  // open: cin, cout
  Register #(.width(16)) MAR (.clk(clock_1_out), .Q(MAR_q));  // open: D, en, clr
  Register #(.width(16)) MDR (.clk(clock_1_out), .Q(MDR_q));  // open: D, en, clr
  Register #(.width(16)) MBR (.clk(clock_1_out), .Q(MBR_q));  // open: D, en, clr
  Register #(.width(16)) MLR (.clk(clock_1_out), .Q(MLR_q));  // open: D, en, clr
  Register #(.width(16)) IR0 (.D(ram_1_dout), .en(and_1_out), .clk(clock_1_out), .Q(IR0_q));  // open: clr
  S_R_Flip_Flop MODE (.clk(clock_1_out), .Q(MODE_q), .reset(undriven_2), .preset(undriven));  // open: S, R, Qn
  Multiplexer #(.width(16)) multiplexer_1 (.in0(PC_q), .in1(MAR_q), .out(multiplexer_1_out), .sel(1'b0));
  Adder #(.width(16)) adder_2 (.a(MBR_q), .b(MLR_q), .out(adder_2_out));  // open: cin, cout
  Comparator #(.width(16)) comparator_1 (.a(MAR_q), .b(MBR_q), .gt(comparator_1_gt), .eq(comparator_1_eq));  // open: lt
  Comparator #(.width(16)) comparator_2 (.a(MAR_q), .b(adder_2_out), .lt(comparator_2_lt));  // open: gt, eq
  and and_5 (and_5_out, comparator_1_gt, comparator_1_eq);
  and and_6 (and_6_out, and_5_out, comparator_2_lt);
  not not_3 (not_3_out, IR0_q[0]);
  not not_4 (not_4_out, IR0_q[1]);
  not not_5 (not_5_out, IR0_q[2]);
  not not_6 (not_6_out, IR0_q[3]);
  not not_7 (not_7_out, IR0_q[4]);
  not not_8 (not_8_out, IR0_q[5]);
  not not_9 (not_9_out, IR0_q[6]);
  not not_10 (not_10_out, IR0_q[7]);
  not not_11 (not_11_out, IR0_q[8]);
  not not_12 (not_12_out, IR0_q[9]);
  not not_13 (not_13_out, IR0_q[10]);
  not not_14 (not_14_out, IR0_q[11]);
  not not_15 (not_15_out, IR0_q[12]);
  not not_16 (not_16_out, IR0_q[13]);
  not not_17 (not_17_out, IR0_q[14]);
  not not_18 (not_18_out, IR0_q[15]);
  // AND_Gate and_7 has open pins: in0=IR0_q[15], in1=IR0_q[14], out=open
  // AND_Gate and_8 has open pins: in0=not_17_out, in1=IR0_q[15], out=open
  // NOT_Gate not_19 has open pins: in=and_6_out, out=open
  // AND_Gate and_9 has open pins: in0=not_18_out, in1=IR0_q[14], out=open
  // AND_Gate and_10 has open pins: in0=not_18_out, in1=not_17_out, out=open
  RAM #(.addrWidth(16), .asyncread("true"), .dataWidth(16)) ram_1 (
    .addr(multiplexer_1_out), .we(1'b0), .oe(and_1_out), .clk(clock_1_out), .din(MDR_q), .dout(ram_1_dout));
endmodule
